# Fritzing sketch Schema (saved by Fritzing 0.9.3b)
breadboards: 1

parts:
  J1 = STM32 Nucleo boards
  hc-sr04_SOL = hc-sr04
  R1 = Resistor [tolerance=±5% resistance=1 package="2010 [SMD]"]
  R2 = Resistor [tolerance=±5% resistance=2.2 package="2010 [SMD]"]
  J2 = Basic Servo
  VCC1 = Battery  # not connected
  5Volt_Regulator = Voltage Regulator LM1117 [package=sot223]  # not connected

nets:
  N1: J1.D8, hc-sr04_SOL.Trig
  N2: J1.D6_PWM, R1.Pin_0, R2.Pin_0
  GND: J1.GND, hc-sr04_SOL.GND, R2.Pin_1, J2.gnd
  VCC: hc-sr04_SOL.VCC, J2.vcc
  N3: hc-sr04_SOL.Echo, R1.Pin_1

custom parts:
  Battery: Your standard 2x 18650 battery pack (7.4 Volts)
